// Logisim project root.circ as structural Verilog
module main (
);

  wire button_1_out, clk, controlpath_1_load, controlpath_1_store;
  wire [7:0] adder_1_out, datapath_1_p3, datapath_1_p4, ram_1_dout, register_1_q;
  wire [23:0] rom_1_data;

  Clock clock_1 (.out(clk));
  Register register_1 (.D(adder_1_out), .Q(register_1_q), .clk(clk));  // open: en, clr
  Adder adder_1 (.a(register_1_q), .b(8'h1), .out(adder_1_out));  // open: cin, cout
  ROM #(.dataWidth(24)) rom_1 (.addr(register_1_q), .data(rom_1_data));
  // DataPath datapath_1: pin names not known; wires that end beside it: rom_1_data[15:0], clk, datapath_1_p3, datapath_1_p4
  ControlPath controlpath_1 (.Opcode(rom_1_data[19:16]), .Load(controlpath_1_load), .Store(controlpath_1_store));
  Button button_1 (.out(button_1_out));
  RAM #(.clearpin("true")) ram_1 (
    .addr(datapath_1_p3), .we(controlpath_1_store), .oe(controlpath_1_load), .clk(clk), .din(datapath_1_p4),
    .dout(ram_1_dout), .clr(button_1_out));
  // Pins of 20 and 24 bits meet at rom_1_data

  // Notes on the sheet:
  //   contents of rom_1 (hex, n*v repeats v):
  //   440003 410000 420100 830100 410101 420201 930200
endmodule

module ControlPath (
  input  [3:0] Opcode,
  output Load,
  output Store
);

  not not_1 (Load, Opcode[0]);

  assign Store = 1'b1;
endmodule

module DataPath (
  input  [7:0] DataIn,
  input  selDataIn,
  input  [15:0] Params,
  input  clk,
  input  selDataOut,
  output [7:0] Address,
  output [7:0] DataOut
);

  wire [7:0] multiplexer_1_out, register_1_q;

  Multiplexer #(.width(8)) multiplexer_1 (.in0(DataIn), .in1(Params[7:0]), .out(multiplexer_1_out), .sel(selDataIn));
  Register register_1 (.D(multiplexer_1_out), .Q(register_1_q), .clk(clk));  // open: en, clr
  ULA ula_1 ();
  Multiplexer #(.width(8)) multiplexer_2 (.in0(multiplexer_1_out), .in1(register_1_q), .out(DataOut), .sel(selDataOut));

  assign Address = Params[15:8];
endmodule
